# Fritzing sketch Blinking Led (saved by Fritzing 0.9.3b)
breadboards: 1

parts:
  R1 = Resistor [tolerance=±5% resistance=220 package="2512 [SMD]"]
  LED1 = smd LED [color="Red (633nm)" package="1206 [SMD]"]
  Atmel's_Atmega32L_Microchip1 = AVR-Atmega32 [package="DIP (Dual Inline)"]

nets:
  N1: R1.Pin_0, LED1.anode
  N2: R1.Pin_1, Atmel's_Atmega32L_Microchip1.pin_1
  N3: LED1.cathode, Atmel's_Atmega32L_Microchip1.pin_11, Atmel's_Atmega32L_Microchip1.pin_31
  N4: Atmel's_Atmega32L_Microchip1.pin_10, Atmel's_Atmega32L_Microchip1.pin_32

notes:
  +5 V
  0 V
  1
  20
  21
  40
  11
  10
  -ve
  +ve
  32
  31

custom parts:
  AVR-Atmega32: Atmel's Atmega32. A beast of an 8 bit microchip to behold! This is not your dad's arduino chip! Also the DIP version of the microchip that is at the helm of the Arduino Mega. For more info, consult the datasheet: http://www.atmel.com/dyn/resources/prod_documents/doc2503.pdf
